# Fritzing sketch Soracom_PIR (saved by Fritzing 0.9.3b)

parts:
  U1 = MLX90614 [package=to-39]
  Part1 = LilyPad Arduino USB
  V3 = DC Power [voltage=3.3V]

nets:
  N1: U1.PWM_SDA, Part1.D3
  3.3V: U1.VDD, Part1.3V3
  VSS: U1.VSS, Part1.GND, V3.V-
  N2: Part1.A4, V3.V+
